# Fritzing sketch Untitled Sketch (saved by Fritzing 0.9.3b)

parts:
  元件1 = Arduino Pro Mini v13  # not connected
  U1 = L9110 H-bridge module [part_number="L9110 H-bridge"]
  M1 = DC Motor
  M2 = DC Motor

nets:
  N1: U1.MOTOR_A-A, M2.pin_2
  N2: U1.MOTOR_A-B, M2.pin_1
  N3: U1.MOTOR_B-A, M1.pin_2
  N4: U1.MOTOR_B-B, M1.pin_1
